// Logisim project projetoic.circ as structural Verilog
module somadorCompleto (
  input  A,
  input  B,
  input  C,
  output Soma,
  output Carry_Out
);

  wire and_1_out, and_2_out, and_3_out, and_4_out, not_1_out, not_2_out, not_3_out, xor_1_out;

  not not_1 (not_1_out, A);
  not not_2 (not_2_out, B);
  not not_3 (not_3_out, C);
  xor xor_1 (xor_1_out, A, B);
  and and_1 (and_1_out, not_1_out, B, C);
  and and_2 (and_2_out, A, not_2_out, C);
  and and_3 (and_3_out, A, B, not_3_out);
  and and_4 (and_4_out, A, B, C);
  xor xor_2 (Soma, xor_1_out, C);
  or or_1 (Carry_Out, and_1_out, and_2_out, and_3_out, and_4_out);

  // Notes on the sheet:
  //   Somador Completo
endmodule

module main (
  input  Controle,
  input  A,
  input  A_2,
  input  B,
  input  B_2,
  input  Controle_2,
  input  in_7,
  input  A_3,
  input  B_3,
  input  in_10,
  input  A0,
  input  A1,
  input  Controle_3,
  input  B0,
  input  B1,
  input  Controle_4,
  input  Controle_5,
  input  Controle_6,
  output out_19,
  output out_20
);

  wire multiplex_1_saida, multiplex_2_saida, multiplex_3_saida, multiplex_4_saida, multiplex_5_saida,
       multiplex_6_saida, multiplicadorcompleto_1_r0, multiplicadorcompleto_1_r1, multiplicadorcompleto_1_r2,
       multiplicadorcompleto_1_r3, somadorcompleto_1_carry_out, somadorcompleto_1_soma,
       somadorcompleto_2_soma, subtrator_full_1_out_4, subtrator_full_1_out_5, subtrator_full_2_out_4;

  somadorCompleto somadorcompleto_1 (
    .A(A), .B(B), .C(1'b0), .Soma(somadorcompleto_1_soma), .Carry_Out(somadorcompleto_1_carry_out));
  multiplicadorCompleto multiplicadorcompleto_1 (
    .A0(A0), .A1(A1), .B0(B0), .B1(B1), .R0(multiplicadorcompleto_1_r0), .R1(multiplicadorcompleto_1_r1),
    .R2(multiplicadorcompleto_1_r2), .R3(multiplicadorcompleto_1_r3));
  somadorCompleto somadorcompleto_2 (
    .A(A_2), .B(B_2), .C(somadorcompleto_1_carry_out), .Soma(somadorcompleto_2_soma), .Carry_Out(out_19));
  subtrator_full subtrator_full_1 (
    .in_1(A_3), .in_2(B_3), .in_3(1'b0), .out_4(subtrator_full_1_out_4), .out_5(subtrator_full_1_out_5));
  subtrator_full subtrator_full_2 (
    .in_1(in_7), .in_2(in_10), .in_3(subtrator_full_1_out_5), .out_4(subtrator_full_2_out_4), .out_5(out_20));
  multiplex multiplex_1 (.E0(multiplicadorcompleto_1_r0), .C(Controle_3), .Saida(multiplex_1_saida));  // open: E1
  multiplex multiplex_2 (.E0(multiplicadorcompleto_1_r1), .C(Controle_4), .Saida(multiplex_2_saida));  // open: E1
  multiplex multiplex_3 (.E0(multiplicadorcompleto_1_r2), .C(Controle_5), .Saida(multiplex_3_saida));  // open: E1
  multiplex multiplex_4 (.E0(multiplicadorcompleto_1_r3), .C(Controle_6), .Saida(multiplex_4_saida));  // open: E1
  multiplex multiplex_5 (
    .E0(somadorcompleto_1_soma), .E1(subtrator_full_1_out_4), .C(Controle), .Saida(multiplex_5_saida));
  multiplex multiplex_6 (
    .E0(somadorcompleto_2_soma), .E1(subtrator_full_2_out_4), .C(Controle_2), .Saida(multiplex_6_saida));
  LED led_1 (.in(multiplex_5_saida));
  LED led_2 (.in(multiplex_6_saida));
  LED led_3 (.in(multiplex_1_saida));
  LED led_4 (.in(multiplex_2_saida));
  LED led_5 (.in(multiplex_3_saida));
  LED led_6 (.in(multiplex_4_saida));

  // Notes on the sheet:
  //   Somador Completo
  //   Subtrator Completo
  //   Multiplicador Completo
  //   Divisor Completo
endmodule

module multiplex (
  input  E0,
  input  E1,
  input  C,
  output Saida
);

  wire and_1_out, and_2_out, not_1_out;

  not not_1 (not_1_out, C);
  and and_1 (and_1_out, E0, not_1_out);
  and and_2 (and_2_out, E1, C);
  or or_1 (Saida, and_1_out, and_2_out);
endmodule

module meioMultiplicador (
  input  A0,
  input  A1,
  input  B0,
  input  B1,
  output P0,
  output P1,
  output P2,
  output P3
);

  and and_1 (P0, A0, B0);
  and and_2 (P1, A1, B0);
  and and_3 (P2, A0, B1);
  and and_4 (P3, A1, B1);
endmodule

module meioSomador (
  input  A,
  input  B,
  output S,
  output C
);

  xor xor_1 (S, A, B);
  and and_1 (C, A, B);
endmodule

module multiplicadorCompleto (
  input  A0,
  input  A1,
  input  B0,
  input  B1,
  output R0,
  output R1,
  output R2,
  output R3
);

  wire meiomultiplicador_1_p1, meiomultiplicador_1_p2, meiomultiplicador_1_p3, meiosomador_1_c;

  meioMultiplicador meiomultiplicador_1 (
    .A0(A0), .A1(A1), .B0(B0), .B1(B1), .P0(R0), .P1(meiomultiplicador_1_p1), .P2(meiomultiplicador_1_p2),
    .P3(meiomultiplicador_1_p3));
  meioSomador meiosomador_1 (.A(meiomultiplicador_1_p1), .B(meiomultiplicador_1_p2), .S(R1), .C(meiosomador_1_c));
  meioSomador meiosomador_2 (.A(meiomultiplicador_1_p3), .B(meiosomador_1_c), .S(R2), .C(R3));
endmodule

module subtrator_meio (
  input  in_1,
  input  in_2,
  output out_3,
  output out_4
);

  wire not_1_out;

  not not_1 (not_1_out, in_1);
  or or_1 (out_3, in_1, in_2);
  and and_1 (out_4, not_1_out, in_2);
endmodule

module subtrator_full (
  input  in_1,
  input  in_2,
  input  in_3,
  output out_4,
  output out_5
);

  wire and_1_out, and_2_out, and_3_out, not_1_out, xor_1_out;

  not not_1 (not_1_out, in_1);
  xor xor_1 (xor_1_out, in_1, in_2);
  and and_1 (and_1_out, not_1_out, in_2);
  and and_2 (and_2_out, not_1_out, in_3);
  and and_3 (and_3_out, in_2, in_3);
  xor xor_2 (out_4, xor_1_out, in_3);
  or or_1 (out_5, and_1_out, and_2_out, and_3_out);
endmodule
